# Fritzing sketch openHelmet (saved by Fritzing 0.9.2b)
breadboards: 1

parts:
  Raspberry_Pi1 = Raspberry Pi 2
  Grove1 = Grove 3 Axis Digital Accelerometer 16g
  LED1 = LEDs [package=led10mm]
  LED2 = LEDs [package=led10mm]
  R1 = Resistor [tolerance=±5% resistance=220 package=THT]
  R2 = Resistor [tolerance=±5% resistance=220 package=THT]

nets:
  3V3: Raspberry_Pi1.3v3, Grove1.VCC
  N1: Raspberry_Pi1.GPIO2, Grove1.SDA
  N2: Raspberry_Pi1.GPIO3, Grove1.SCL
  N3: Raspberry_Pi1.GPIO17, R1.Pin_0
  N4: Raspberry_Pi1.GPIO22, R2.Pin_0
  GND: Raspberry_Pi1.GND, Grove1.GND
  N5: LED1.A, R1.Pin_1
  N6: LED1.C, LED2.C
  N7: LED2.A, R2.Pin_1
